# Fritzing sketch arduino-keyboard (saved by Fritzing 0.9.4)
breadboards: 1

parts:
  Part1 = Arduino Micro (Rev3)
  S2 = Pushbutton [package="[SMD]"]
  S3 = Pushbutton [package="[SMD]"]
  S4 = Pushbutton [package="[SMD]"]
  S5 = Pushbutton [package="[SMD]"]
  S6 = Pushbutton [package="[SMD]"]

nets:
  N1: Part1.GND, S2.Pin_1, S2.Pin_2, S3.Pin_1, S3.Pin_2, S4.Pin_1, S4.Pin_2, S5.Pin_1, S5.Pin_2, S6.Pin_1, S6.Pin_2
  N2: Part1.D2/SDA, S2.Pin_3, S2.Pin_4
  N3: Part1.D3/SCL, S3.Pin_3, S3.Pin_4
  N4: Part1.D4_PWM/A6, S4.Pin_3, S4.Pin_4
  N5: Part1.D5_PWM, S5.Pin_3, S5.Pin_4
  N6: Part1.D6_PWM/A7, S6.Pin_3, S6.Pin_4
